# Fritzing sketch MQTT-Temperature-Publisher (saved by Fritzing 0.9.3b)
breadboards: 1

parts:
  WeMos_D1_Mini1 = WeMos D1 Mini
  DS1 = DS18B20 1-Wire Temperature Sensor [part_number=DS18B20]
  R1 = Resistor [tolerance=±5% resistance=4.7k package="0805 [SMD]"]

nets:
  3V3: WeMos_D1_Mini1.3V3, DS1.VDD, R1.Pin_0
  N1: WeMos_D1_Mini1.D4, DS1.DQ, R1.Pin_1
  N2: WeMos_D1_Mini1.G, DS1.GND

notes:
  4,7 kOhm PullUp
  Resistor
